// Logisim project VDUTest.circ as structural Verilog: 1 circuit, main circuit main
module main (
  input  [63:0] in_1,
  input  in_2,
  input  [63:0] in_3,
  input  [63:0] in_4,
  input  [63:0] in_5,
  input  [63:0] in_6,
  input  [63:0] in_7,
  input  [63:0] in_8,
  input  [63:0] in_9
);

  _7_Segment_Display u_7_segment_display_1 (
    .g(in_1[63]), .f(in_1[62]), .a(in_1[61]), .b(in_1[60]), .e(in_4[63]), .d(in_4[62]), .c(in_4[61]),
    .dp(in_4[60]));
  _7_Segment_Display u_7_segment_display_2 (
    .g(in_3[63]), .f(in_3[62]), .a(in_3[61]), .b(in_3[60]), .e(in_6[63]), .d(in_6[62]), .c(in_6[61]),
    .dp(in_6[60]));
  _7_Segment_Display u_7_segment_display_3 (
    .g(in_5[63]), .f(in_5[62]), .a(in_5[61]), .b(in_5[60]), .e(in_8[63]), .d(in_8[62]), .c(in_8[61]),
    .dp(in_8[60]));
  _7_Segment_Display u_7_segment_display_4 (
    .g(in_7[63]), .f(in_7[62]), .a(in_7[61]), .b(in_7[60]), .e(in_9[63]), .d(in_9[62]), .c(in_9[61]),
    .dp(in_9[60]));
  _7_Segment_Display u_7_segment_display_5 (
    .g(in_1[59]), .f(in_1[58]), .a(in_1[57]), .b(in_1[56]), .e(in_4[59]), .d(in_4[58]), .c(in_4[57]),
    .dp(in_4[56]));
  _7_Segment_Display u_7_segment_display_6 (
    .g(in_1[55]), .f(in_1[54]), .a(in_1[53]), .b(in_1[52]), .e(in_4[55]), .d(in_4[54]), .c(in_4[53]),
    .dp(in_4[52]));
  _7_Segment_Display u_7_segment_display_7 (
    .g(in_3[59]), .f(in_3[58]), .a(in_3[57]), .b(in_3[56]), .e(in_6[59]), .d(in_6[58]), .c(in_6[57]),
    .dp(in_6[56]));
  _7_Segment_Display u_7_segment_display_8 (
    .g(in_3[55]), .f(in_3[54]), .a(in_3[53]), .b(in_3[52]), .e(in_6[55]), .d(in_6[54]), .c(in_6[53]),
    .dp(in_6[52]));
  _7_Segment_Display u_7_segment_display_9 (
    .g(in_5[59]), .f(in_5[58]), .a(in_5[57]), .b(in_5[56]), .e(in_8[59]), .d(in_8[58]), .c(in_8[57]),
    .dp(in_8[56]));
  _7_Segment_Display u_7_segment_display_10 (
    .g(in_5[55]), .f(in_5[54]), .a(in_5[53]), .b(in_5[52]), .e(in_8[55]), .d(in_8[54]), .c(in_8[53]),
    .dp(in_8[52]));
  _7_Segment_Display u_7_segment_display_11 (
    .g(in_7[59]), .f(in_7[58]), .a(in_7[57]), .b(in_7[56]), .e(in_9[59]), .d(in_9[58]), .c(in_9[57]),
    .dp(in_9[56]));
  _7_Segment_Display u_7_segment_display_12 (
    .g(in_7[55]), .f(in_7[54]), .a(in_7[53]), .b(in_7[52]), .e(in_9[55]), .d(in_9[54]), .c(in_9[53]),
    .dp(in_9[52]));
  _7_Segment_Display u_7_segment_display_13 (
    .g(in_1[51]), .f(in_1[50]), .a(in_1[49]), .b(in_1[48]), .e(in_4[51]), .d(in_4[50]), .c(in_4[49]),
    .dp(in_4[48]));
  _7_Segment_Display u_7_segment_display_14 (
    .g(in_1[47]), .f(in_1[46]), .a(in_1[45]), .b(in_1[44]), .e(in_4[47]), .d(in_4[46]), .c(in_4[45]),
    .dp(in_4[44]));
  _7_Segment_Display u_7_segment_display_15 (
    .g(in_3[51]), .f(in_3[50]), .a(in_3[49]), .b(in_3[48]), .e(in_6[51]), .d(in_6[50]), .c(in_6[49]),
    .dp(in_6[48]));
  _7_Segment_Display u_7_segment_display_16 (
    .g(in_3[47]), .f(in_3[46]), .a(in_3[45]), .b(in_3[44]), .e(in_6[47]), .d(in_6[46]), .c(in_6[45]),
    .dp(in_6[44]));
  _7_Segment_Display u_7_segment_display_17 (
    .g(in_5[51]), .f(in_5[50]), .a(in_5[49]), .b(in_5[48]), .e(in_8[51]), .d(in_8[50]), .c(in_8[49]),
    .dp(in_8[48]));
  _7_Segment_Display u_7_segment_display_18 (
    .g(in_5[47]), .f(in_5[46]), .a(in_5[45]), .b(in_5[44]), .e(in_8[47]), .d(in_8[46]), .c(in_8[45]),
    .dp(in_8[44]));
  _7_Segment_Display u_7_segment_display_19 (
    .g(in_7[51]), .f(in_7[50]), .a(in_7[49]), .b(in_7[48]), .e(in_9[51]), .d(in_9[50]), .c(in_9[49]),
    .dp(in_9[48]));
  _7_Segment_Display u_7_segment_display_20 (
    .g(in_7[47]), .f(in_7[46]), .a(in_7[45]), .b(in_7[44]), .e(in_9[47]), .d(in_9[46]), .c(in_9[45]),
    .dp(in_9[44]));
  Hex_Digit_Display hex_digit_display_1 ();  // open: value, dp
  _7_Segment_Display u_7_segment_display_21 (
    .g(in_1[43]), .f(in_1[42]), .a(in_1[41]), .b(in_1[40]), .e(in_4[43]), .d(in_4[42]), .c(in_4[41]),
    .dp(in_4[40]));
  _7_Segment_Display u_7_segment_display_22 (
    .g(in_1[39]), .f(in_1[38]), .a(in_1[37]), .b(in_1[36]), .e(in_4[39]), .d(in_4[38]), .c(in_4[37]),
    .dp(in_4[36]));
  _7_Segment_Display u_7_segment_display_23 (
    .g(in_3[43]), .f(in_3[42]), .a(in_3[41]), .b(in_3[40]), .e(in_6[43]), .d(in_6[42]), .c(in_6[41]),
    .dp(in_6[40]));
  _7_Segment_Display u_7_segment_display_24 (
    .g(in_3[39]), .f(in_3[38]), .a(in_3[37]), .b(in_3[36]), .e(in_6[39]), .d(in_6[38]), .c(in_6[37]),
    .dp(in_6[36]));
  _7_Segment_Display u_7_segment_display_25 (
    .g(in_5[43]), .f(in_5[42]), .a(in_5[41]), .b(in_5[40]), .e(in_8[43]), .d(in_8[42]), .c(in_8[41]),
    .dp(in_8[40]));
  _7_Segment_Display u_7_segment_display_26 (
    .g(in_5[39]), .f(in_5[38]), .a(in_5[37]), .b(in_5[36]), .e(in_8[39]), .d(in_8[38]), .c(in_8[37]),
    .dp(in_8[36]));
  _7_Segment_Display u_7_segment_display_27 (
    .g(in_7[43]), .f(in_7[42]), .a(in_7[41]), .b(in_7[40]), .e(in_9[43]), .d(in_9[42]), .c(in_9[41]),
    .dp(in_9[40]));
  _7_Segment_Display u_7_segment_display_28 (
    .g(in_7[39]), .f(in_7[38]), .a(in_7[37]), .b(in_7[36]), .e(in_9[39]), .d(in_9[38]), .c(in_9[37]),
    .dp(in_9[36]));
  _7_Segment_Display u_7_segment_display_29 (
    .g(in_1[35]), .f(in_1[34]), .a(in_1[33]), .b(in_1[32]), .e(in_4[35]), .d(in_4[34]), .c(in_4[33]),
    .dp(in_4[32]));
  _7_Segment_Display u_7_segment_display_30 (
    .g(in_1[31]), .f(in_1[30]), .a(in_1[29]), .b(in_1[28]), .e(in_4[31]), .d(in_4[30]), .c(in_4[29]),
    .dp(in_4[28]));
  _7_Segment_Display u_7_segment_display_31 (
    .g(in_3[35]), .f(in_3[34]), .a(in_3[33]), .b(in_3[32]), .e(in_6[35]), .d(in_6[34]), .c(in_6[33]),
    .dp(in_6[32]));
  _7_Segment_Display u_7_segment_display_32 (
    .g(in_3[31]), .f(in_3[30]), .a(in_3[29]), .b(in_3[28]), .e(in_6[31]), .d(in_6[30]), .c(in_6[29]),
    .dp(in_6[28]));
  _7_Segment_Display u_7_segment_display_33 (
    .g(in_5[35]), .f(in_5[34]), .a(in_5[33]), .b(in_5[32]), .e(in_8[35]), .d(in_8[34]), .c(in_8[33]),
    .dp(in_8[32]));
  _7_Segment_Display u_7_segment_display_34 (
    .g(in_5[31]), .f(in_5[30]), .a(in_5[29]), .b(in_5[28]), .e(in_8[31]), .d(in_8[30]), .c(in_8[29]),
    .dp(in_8[28]));
  _7_Segment_Display u_7_segment_display_35 (
    .g(in_7[35]), .f(in_7[34]), .a(in_7[33]), .b(in_7[32]), .e(in_9[35]), .d(in_9[34]), .c(in_9[33]),
    .dp(in_9[32]));
  _7_Segment_Display u_7_segment_display_36 (
    .g(in_7[31]), .f(in_7[30]), .a(in_7[29]), .b(in_7[28]), .e(in_9[31]), .d(in_9[30]), .c(in_9[29]),
    .dp(in_9[28]));
  _7_Segment_Display u_7_segment_display_37 (
    .g(in_1[27]), .f(in_1[26]), .a(in_1[25]), .b(in_1[24]), .e(in_4[27]), .d(in_4[26]), .c(in_4[25]),
    .dp(in_4[24]));
  _7_Segment_Display u_7_segment_display_38 (
    .g(in_1[23]), .f(in_1[22]), .a(in_1[21]), .b(in_1[20]), .e(in_4[23]), .d(in_4[22]), .c(in_4[21]),
    .dp(in_4[20]));
  _7_Segment_Display u_7_segment_display_39 (
    .g(in_3[27]), .f(in_3[26]), .a(in_3[25]), .b(in_3[24]), .e(in_6[27]), .d(in_6[26]), .c(in_6[25]),
    .dp(in_6[24]));
  _7_Segment_Display u_7_segment_display_40 (
    .g(in_3[23]), .f(in_3[22]), .a(in_3[21]), .b(in_3[20]), .e(in_6[23]), .d(in_6[22]), .c(in_6[21]),
    .dp(in_6[20]));
  _7_Segment_Display u_7_segment_display_41 (
    .g(in_5[27]), .f(in_5[26]), .a(in_5[25]), .b(in_5[24]), .e(in_8[27]), .d(in_8[26]), .c(in_8[25]),
    .dp(in_8[24]));
  _7_Segment_Display u_7_segment_display_42 (
    .g(in_5[23]), .f(in_5[22]), .a(in_5[21]), .b(in_5[20]), .e(in_8[23]), .d(in_8[22]), .c(in_8[21]),
    .dp(in_8[20]));
  _7_Segment_Display u_7_segment_display_43 (
    .g(in_7[27]), .f(in_7[26]), .a(in_7[25]), .b(in_7[24]), .e(in_9[27]), .d(in_9[26]), .c(in_9[25]),
    .dp(in_9[24]));
  _7_Segment_Display u_7_segment_display_44 (
    .g(in_7[23]), .f(in_7[22]), .a(in_7[21]), .b(in_7[20]), .e(in_9[23]), .d(in_9[22]), .c(in_9[21]),
    .dp(in_9[20]));
  DotMatrix dotmatrix_1 ();  // open: col0, col1, col2, col3, col4
  _7_Segment_Display u_7_segment_display_45 (
    .g(in_1[19]), .f(in_1[18]), .a(in_1[17]), .b(in_1[16]), .e(in_4[19]), .d(in_4[18]), .c(in_4[17]),
    .dp(in_4[16]));
  _7_Segment_Display u_7_segment_display_46 (
    .g(in_1[15]), .f(in_1[14]), .a(in_1[13]), .b(in_1[12]), .e(in_4[15]), .d(in_4[14]), .c(in_4[13]),
    .dp(in_4[12]));
  _7_Segment_Display u_7_segment_display_47 (
    .g(in_3[19]), .f(in_3[18]), .a(in_3[17]), .b(in_3[16]), .e(in_6[19]), .d(in_6[18]), .c(in_6[17]),
    .dp(in_6[16]));
  _7_Segment_Display u_7_segment_display_48 (
    .g(in_3[15]), .f(in_3[14]), .a(in_3[13]), .b(in_3[12]), .e(in_6[15]), .d(in_6[14]), .c(in_6[13]),
    .dp(in_6[12]));
  _7_Segment_Display u_7_segment_display_49 (
    .g(in_5[19]), .f(in_5[18]), .a(in_5[17]), .b(in_5[16]), .e(in_8[19]), .d(in_8[18]), .c(in_8[17]),
    .dp(in_8[16]));
  _7_Segment_Display u_7_segment_display_50 (
    .g(in_5[15]), .f(in_5[14]), .a(in_5[13]), .b(in_5[12]), .e(in_8[15]), .d(in_8[14]), .c(in_8[13]),
    .dp(in_8[12]));
  _7_Segment_Display u_7_segment_display_51 (
    .g(in_7[19]), .f(in_7[18]), .a(in_7[17]), .b(in_7[16]), .e(in_9[19]), .d(in_9[18]), .c(in_9[17]),
    .dp(in_9[16]));
  _7_Segment_Display u_7_segment_display_52 (
    .g(in_7[15]), .f(in_7[14]), .a(in_7[13]), .b(in_7[12]), .e(in_9[15]), .d(in_9[14]), .c(in_9[13]),
    .dp(in_9[12]));
  // RGB_Video #(.height(64), .width(64)) rgb_video_1: pin names not known
  _7_Segment_Display u_7_segment_display_53 (
    .g(in_1[11]), .f(in_1[10]), .a(in_1[9]), .b(in_1[8]), .e(in_4[11]), .d(in_4[10]), .c(in_4[9]),
    .dp(in_4[8]));
  _7_Segment_Display u_7_segment_display_54 (
    .g(in_1[7]), .f(in_1[6]), .a(in_1[5]), .b(in_1[4]), .e(in_4[7]), .d(in_4[6]), .c(in_4[5]), .dp(in_4[4]));
  _7_Segment_Display u_7_segment_display_55 (
    .g(in_3[11]), .f(in_3[10]), .a(in_3[9]), .b(in_3[8]), .e(in_6[11]), .d(in_6[10]), .c(in_6[9]),
    .dp(in_6[8]));
  _7_Segment_Display u_7_segment_display_56 (
    .g(in_3[7]), .f(in_3[6]), .a(in_3[5]), .b(in_3[4]), .e(in_6[7]), .d(in_6[6]), .c(in_6[5]), .dp(in_6[4]));
  _7_Segment_Display u_7_segment_display_57 (
    .g(in_5[11]), .f(in_5[10]), .a(in_5[9]), .b(in_5[8]), .e(in_8[11]), .d(in_8[10]), .c(in_8[9]),
    .dp(in_8[8]));
  _7_Segment_Display u_7_segment_display_58 (
    .g(in_5[7]), .f(in_5[6]), .a(in_5[5]), .b(in_5[4]), .e(in_8[7]), .d(in_8[6]), .c(in_8[5]), .dp(in_8[4]));
  _7_Segment_Display u_7_segment_display_59 (
    .g(in_7[11]), .f(in_7[10]), .a(in_7[9]), .b(in_7[8]), .e(in_9[11]), .d(in_9[10]), .c(in_9[9]),
    .dp(in_9[8]));
  _7_Segment_Display u_7_segment_display_60 (
    .g(in_7[7]), .f(in_7[6]), .a(in_7[5]), .b(in_7[4]), .e(in_9[7]), .d(in_9[6]), .c(in_9[5]), .dp(in_9[4]));
  _7_Segment_Display u_7_segment_display_61 (
    .g(in_1[3]), .f(in_1[2]), .a(in_1[1]), .b(in_1[0]), .e(in_4[3]), .d(in_4[2]), .c(in_4[1]), .dp(in_4[0]));
  _7_Segment_Display u_7_segment_display_62 (
    .g(in_3[3]), .f(in_3[2]), .a(in_3[1]), .b(in_3[0]), .e(in_6[3]), .d(in_6[2]), .c(in_6[1]), .dp(in_6[0]));
  _7_Segment_Display u_7_segment_display_63 (
    .g(in_5[3]), .f(in_5[2]), .a(in_5[1]), .b(in_5[0]), .e(in_8[3]), .d(in_8[2]), .c(in_8[1]), .dp(in_8[0]));
  _7_Segment_Display u_7_segment_display_64 (
    .g(in_7[3]), .f(in_7[2]), .a(in_7[1]), .b(in_7[0]), .e(in_9[3]), .d(in_9[2]), .c(in_9[1]), .dp(in_9[0]));
endmodule
